// Digital circuit CPU.dig as structural Verilog
module CPU (
  input  RUN,
  input  [7:0] MCBREAKPOINT,
  input  [7:0] UCBREAKPOINT,
  input  FAST,
  input  SLOW,
  input  MCBSET,
  input  UCBSET
);

  wire A_LD_CDATA, A_OUT_CDATA, ALUA_LD_CDATA, ALUB_LD_CDATA, ALUOP_0, ALUOP_1, ALUR_OUT_CDATA, ALUZ_OUT,
       and_1_out, and_2_out, and_3_out, and_4_out, and_5_out, And_6_pin8, And_6_pin11, and_7_out, and_8_out,
       BREAK, CDATA_LD_0, CDATA_TO_CADDR, CLOCK, clock_1_p6, comparator_1_eq, comparator_2_eq,
       comparator_3_gt, comparator_4_eq, comparator_5_eq, Connect_CDATA_to_CADDR__Tristate_pin1, CPU_ERR,
       CS0, CS1, CS2, decoder_1_out_0, decoder_1_out_1, decoder_1_out_2, decoder_1_out_3, decoder_2_out_0,
       decoder_2_out_1, decoder_2_out_2, decoder_2_out_3, decoder_2_out_4, decoder_2_out_5, decoder_2_out_6,
       decoder_2_out_7, ERROR, fake_carry_1_p2, FROMMBR0, FROMMBR1, FROMMBR2, FROMMBR3, FROMMBR4, FROMMBR5,
       FROMMBR6, FROMMBR7, FROMPC0, FROMPC1, FROMPC2, FROMPC3, FROMPC4, FROMPC5, FROMPC6, FROMPC7,
       FROMXCDATA0, FROMXCDATA1, FROMXCDATA2, FROMXCDATA3, FROMXCDATA4, FROMXCDATA5, FROMXCDATA6,
       FROMXCDATA7, FROMXDATA0, FROMXDATA1, FROMXDATA2, FROMXDATA3, FROMXDATA4, FROMXDATA5, FROMXDATA6,
       FROMXDATA7, HALTED, IR_LD_XDATA, Load_control__Or_pin11, MAR_LD_CADDR, MBR_LD_CDATA, MBR_LD_XDATA,
       MBR_OUT_CDATA, MBR_OUT_XDATA, MEM_LD_XDATA, MEM_OUT_XDATA, Not_2_pin4, Not_2_pin12, Not_3_pin12,
       Not_pin12, or_1_out, Or_5_pin8, PC_INC, PC_LD_CDATA, PC_OUT_CADDR, PC_OUT_CDATA, PC_REL_CDATA, PZ_LD,
       RESET, Route_to_CADDR__Tristate_pin1, Route_to_XDATA__Tristate_pin1, STEP_out, switchdt_1_p3,
       X_LD_CDATA, X_OUT_CDATA, Z, Z_Source___ALU_or_CDATA_pin4, Z_SRC_CDATA, zero_1_p2;
  wire [2:0] lt_CARNEXTSRC_gt;
  wire [3:0] register_1_q, register_1_q_2, register_2_q, register_2_q_2;
  wire [7:0] A, ALUR, CADDR, IR, lt_ALUA_gt, lt_ALUB_gt, lt_CAR_gt, lt_CARNEXT_gt, lt_UPARAM_gt, MAR,
       MODEADDR, OPCODEADDR, X;

  Button STEP (.out(STEP_out));
  Button u_RESET (.out(RESET));
  Seven_Seg_Hex seven_seg_hex_1 (.d(MAR[3:0]), .dp(1'b0));
  Seven_Seg_Hex seven_seg_hex_2 (.d(MAR[7:4]), .dp(1'b0));
  Seven_Seg_Hex seven_seg_hex_3 (.d(A[3:0]), .dp(1'b0));
  Seven_Seg_Hex seven_seg_hex_4 (.d(A[7:4]), .dp(1'b0));
  or or_1 (or_1_out, ERROR, BREAK);
  // SwitchDT switchdt_1: pin names not known; wires that end beside it: FAST, SLOW, switchdt_1_p3
  Seven_Seg_Hex seven_seg_hex_5 (.d({FROMMBR7, FROMMBR6, FROMMBR5, FROMMBR4}), .dp(1'b0));
  Seven_Seg_Hex seven_seg_hex_6 (.d(X[7:4]), .dp(1'b0));
  Comparator #(.Bits(8)) comparator_1 (
    .a(MCBREAKPOINT), .b({FROMPC7, FROMPC6, FROMPC5, FROMPC4, FROMPC3, FROMPC2, FROMPC1, FROMPC0}),
    .eq(comparator_1_eq));  // open: gt, lt
  Comparator #(.Bits(8)) comparator_2 (.a(UCBREAKPOINT), .b(lt_CAR_gt), .eq(comparator_2_eq));  // open: gt, lt
  and and_1 (and_1_out, CS0, MEM_LD_XDATA);
  Comparator #(.Bits(8)) comparator_3 (.a(MAR), .b(8'hf2), .gt(comparator_3_gt));  // open: eq, lt
  Seven_Seg_Hex seven_seg_hex_7 (.d({FROMMBR3, FROMMBR2, FROMMBR1, FROMMBR0}), .dp(1'b0));
  Seven_Seg_Hex seven_seg_hex_8 (.d(X[3:0]), .dp(1'b0));
  and and_2 (and_2_out, MCBSET, comparator_1_eq);
  and and_3 (and_3_out, UCBSET, comparator_2_eq);
  and and_4 (and_4_out, CS2, comparator_3_gt);
  // Clock clock_1: pin names not known; wires that end beside it: RUN, STEP_out, or_1_out, switchdt_1_p3, HALTED, clock_1_p6
  Seven_Seg_Hex seven_seg_hex_9 (.d({FROMPC3, FROMPC2, FROMPC1, FROMPC0}), .dp(1'b0));
  Seven_Seg_Hex seven_seg_hex_10 (.d({FROMPC7, FROMPC6, FROMPC5, FROMPC4}), .dp(1'b0));
  or or_2 (BREAK, and_2_out, and_3_out);
  or or_3 (ERROR, CPU_ERR, and_1_out, and_4_out);
  and and_5 (and_5_out, HALTED, RESET);
  Seven_Seg_Hex seven_seg_hex_11 (.d(IR[7:4]), .dp(1'b0));
  LED led_1 (.in(Z));
  or or_4 (CLOCK, clock_1_p6, and_5_out);
  Seven_Seg_Hex seven_seg_hex_12 (.d(IR[3:0]), .dp(1'b0));
  _7432 Or_5 (
    .pin1(1'b0), .pin2(1'b0), .pin4(1'b0), .pin5(1'b0), .pin7(1'b0), .pin8(Or_5_pin8), .pin9(MEM_OUT_XDATA),
    .pin10(MEM_LD_XDATA), .pin12(1'b0), .pin13(1'b0), .pin14(1'b1));  // open: pin3, pin6, pin11
  PullDown #(.Bits(8)) pulldown_1 (.out(MAR));
  PullDown #(.Bits(8)) pulldown_2 (.out(CADDR));
  Seven_Seg_Hex seven_seg_hex_13 (.d(lt_ALUA_gt[7:4]), .dp(1'b0));
  Seven_Seg_Hex seven_seg_hex_14 (.d(MODEADDR[7:4]), .dp(1'b0));
  Seven_Seg_Hex seven_seg_hex_15 (.d(lt_ALUA_gt[3:0]), .dp(1'b0));
  _7408 And_6 (
    .pin1(1'b0), .pin2(1'b0), .pin4(1'b0), .pin5(1'b0), .pin7(1'b0), .pin8(And_6_pin8), .pin9(MEM_OUT_XDATA),
    .pin10(CS0), .pin11(And_6_pin11), .pin12(CLOCK), .pin13(MEM_LD_XDATA), .pin14(1'b1));  // open: pin3, pin6
  // Address_Decoder address_decoder_1: pin names not known; wires that end beside it: MAR, Or_5_pin8, CS0, CS1, CS2, MAR
  Seven_Seg_Hex seven_seg_hex_16 (.d(MODEADDR[3:0]), .dp(1'b0));
  Seven_Seg_Hex seven_seg_hex_17 (.d(lt_ALUB_gt[3:0]), .dp(1'b0));
  Seven_Seg_Hex seven_seg_hex_18 (.d(lt_ALUB_gt[7:4]), .dp(1'b0));
  // Register MAR: pin names not known; wires that end beside it: CADDR, CLOCK, CADDR, 1'b1, MAR_LD_CADDR, MAR
  Seven_Seg_Hex seven_seg_hex_19 (.d(ALUR[3:0]), .dp(1'b0));
  Seven_Seg_Hex seven_seg_hex_20 (.d(ALUR[7:4]), .dp(1'b0));
  Seven_Seg_Hex seven_seg_hex_21 (.d(OPCODEADDR[3:0]), .dp(1'b0));
  Seven_Seg_Hex seven_seg_hex_22 (.d(OPCODEADDR[7:4]), .dp(1'b0));
  LED led_2 (.in(ALUZ_OUT));
  Decoder #(.Selector_Bits(2)) decoder_1 (
    .sel({ALUOP_1, ALUOP_0}), .out_0(decoder_1_out_0), .out_1(decoder_1_out_1), .out_2(decoder_1_out_2),
    .out_3(decoder_1_out_3));
  LED ADD (.in(decoder_1_out_0));
  LED SUB (.in(decoder_1_out_1));
  LED INC (.in(decoder_1_out_2));
  LED DEC (.in(decoder_1_out_3));
  Seven_Seg_Hex seven_seg_hex_23 (.d(lt_CAR_gt[3:0]), .dp(1'b0));
  Seven_Seg_Hex seven_seg_hex_24 (.d(lt_CAR_gt[7:4]), .dp(1'b0));
  RAMSinglePortSel #(.AddrBits(4), .isProgramMemory("true"), .Bits(8)) RAM (
    .A(MAR[3:0]), .CS(CS1), .WE(And_6_pin11), .OE(MEM_OUT_XDATA),
    .D({FROMXDATA7, FROMXDATA6, FROMXDATA5, FROMXDATA4, FROMXDATA3, FROMXDATA2, FROMXDATA1, FROMXDATA0}));
  ROM #(.AddrBits(8), .Bits(8)) ROM (
    .A(MAR), .sel(And_6_pin8),
    .D({FROMXDATA7, FROMXDATA6, FROMXDATA5, FROMXDATA4, FROMXDATA3, FROMXDATA2, FROMXDATA1, FROMXDATA0}));
  Seven_Seg_Hex seven_seg_hex_25 (.d(lt_CARNEXT_gt[7:4]), .dp(1'b0));
  // Fake_carry fake_carry_1: pin names not known; wires that end beside it: {ALUOP_1, ALUOP_0}, fake_carry_1_p2, ALUR
  Seven_Seg_Hex seven_seg_hex_26 (.d(lt_CARNEXT_gt[3:0]), .dp(1'b0));
  // Zero zero_1: pin names not known; wires that end beside it: ALUR, zero_1_p2
  Seven_Seg_Hex seven_seg_hex_27 (.d(lt_UPARAM_gt[7:4]), .dp(1'b0));
  // Io io_1: pin names not known; wires that end beside it: MAR, {FROMXDATA7, FROMXDATA6, FROMXDATA5, FROMXDATA4, FROMXDATA3, FROMXDATA2, FROMXDATA1, FROMXDATA0}, MEM_LD_XDATA, CLOCK
  ALU alu_1 (
    .AIN(ALUR), .BIN(ALUR), .CIN(fake_carry_1_p2), .LDA(ALUA_LD_CDATA), .LDB(ALUB_LD_CDATA),
    .OUT(ALUR_OUT_CDATA), .OP({ALUOP_1, ALUOP_0}), .CLCK(CLOCK), .Q(ALUR), .ZOUT(ALUZ_OUT),
    .lt_A_gt(lt_ALUA_gt), .lt_B_gt(lt_ALUB_gt));  // open: COUT
  Seven_Seg_Hex seven_seg_hex_28 (.d(lt_UPARAM_gt[3:0]), .dp(1'b0));
  Comparator #(.Bits(8)) comparator_4 (.a(MAR), .b(8'hf0), .eq(comparator_4_eq));  // open: gt, lt
  // Register IR: pin names not known; wires that end beside it: {FROMXDATA7, FROMXDATA6, FROMXDATA5, FROMXDATA4, FROMXDATA3, FROMXDATA2, FROMXDATA1, FROMXDATA0}, CLOCK, {FROMXDATA7, FROMXDATA6, FROMXDATA5, FROMXDATA4, FROMXDATA3, FROMXDATA2, FROMXDATA1, FROMXDATA0}, 1'b1, IR_LD_XDATA, IR
  _74157 Z_Source___ALU_or_CDATA (
    .pin1(Z_SRC_CDATA), .pin2(ALUZ_OUT), .pin3(zero_1_p2), .pin4(Z_Source___ALU_or_CDATA_pin4), .pin5(1'b0),
    .pin6(1'b0), .pin8(1'b0), .pin10(1'b0), .pin11(1'b0), .pin13(1'b0), .pin14(1'b0), .pin15(1'b0),
    .pin16(1'b1));  // open: pin7, pin9, pin12
  Decoder #(.Selector_Bits(3)) decoder_2 (
    .sel(lt_CARNEXTSRC_gt), .out_0(decoder_2_out_0), .out_1(decoder_2_out_1), .out_2(decoder_2_out_2),
    .out_3(decoder_2_out_3), .out_4(decoder_2_out_4), .out_5(decoder_2_out_5), .out_6(decoder_2_out_6),
    .out_7(decoder_2_out_7));
  Seven_Seg_Hex seven_seg_hex_29 (.d(register_1_q_2), .dp(1'b0));
  LED plus_1 (.in(decoder_2_out_0));
  LED p0 (.in(decoder_2_out_1));
  LED p1 (.in(decoder_2_out_2));
  LED p2 (.in(decoder_2_out_3));
  LED uJMPs (.in(decoder_2_out_4));
  LED Reset_2 (.in(decoder_2_out_5));
  LED N_A (.in(decoder_2_out_6));
  LED N_A_2 (.in(decoder_2_out_7));
  Seven_Seg_Hex seven_seg_hex_30 (.d(register_1_q), .dp(1'b0));
  Register #(.Bits(8)) register_1 (
    .D({FROMXDATA7, FROMXDATA6, FROMXDATA5, FROMXDATA4, FROMXDATA3, FROMXDATA2, FROMXDATA1, FROMXDATA0}),
    .C(CLOCK), .en(and_7_out), .Q({register_1_q_2, register_1_q}));
  and and_7 (and_7_out, comparator_4_eq, CS2);
  Comparator #(.Bits(8)) comparator_5 (.a(MAR), .b(8'hf1), .eq(comparator_5_eq));  // open: gt, lt
  PullDown #(.Bits(8)) pulldown_3 (.out({FROMXDATA7, FROMXDATA6, FROMXDATA5, FROMXDATA4, FROMXDATA3, FROMXDATA2, FROMXDATA1, FROMXDATA0}));
  Seven_Seg_Hex seven_seg_hex_31 (.d(register_2_q), .dp(1'b0));
  Seven_Seg_Hex seven_seg_hex_32 (.d(register_2_q_2), .dp(1'b0));
  and and_8 (and_8_out, comparator_5_eq, CS2);
  Register #(.Bits(8)) register_2 (
    .D({FROMXDATA7, FROMXDATA6, FROMXDATA5, FROMXDATA4, FROMXDATA3, FROMXDATA2, FROMXDATA1, FROMXDATA0}),
    .C(CLOCK), .en(and_8_out), .Q({register_2_q_2, register_2_q}));
  Instruction_Decoder Instruction_Decoder (.OPCODE(IR), .MODEADDR(MODEADDR), .OPCODEADDR(OPCODEADDR));
  // P p_1: pin names not known; wires that end beside it: PZ_LD, Z_Source___ALU_or_CDATA_pin4, CLOCK, 1'b0, 1'b0, Z
  // Register A: pin names not known; wires that end beside it: {FROMXDATA7, FROMXDATA6, FROMXDATA5, FROMXDATA4, FROMXDATA3, FROMXDATA2, FROMXDATA1, FROMXDATA0}, CLOCK, ALUR, A_OUT_CDATA, A_LD_CDATA, ALUR, A
  LED led_3 (.in(HALTED));
  LED led_4 (.in(ERROR));
  LED led_5 (.in(BREAK));
  // Register X: pin names not known; wires that end beside it: CLOCK, ALUR, X_OUT_CDATA, X_LD_CDATA, ALUR, X, ALUR
  Control_Unit Control_Unit (
    .MODEADDR(MODEADDR), .OPCODEADDR(OPCODEADDR), .Z(Z), .RESET(RESET), .CLOCK(CLOCK),
    .CDATA_LD_0(CDATA_LD_0), .CDATA_TO_CADDR(CDATA_TO_CADDR), .MEM_LD_XDATA(MEM_LD_XDATA),
    .MEM_OUT_XDATA(MEM_OUT_XDATA), .IR_LD_XDATA(IR_LD_XDATA), .MBR_LD_XDATA(MBR_LD_XDATA),
    .MBR_OUT_XDATA(MBR_OUT_XDATA), .MBR_LD_CDATA(MBR_LD_CDATA), .MBR_OUT_CDATA(MBR_OUT_CDATA),
    .MAR_LD_CADDR(MAR_LD_CADDR), .PC_INC(PC_INC), .PC_REL_CDATA(PC_REL_CDATA), .PC_LD_CDATA(PC_LD_CDATA),
    .PCL_OUT_CDATA(PC_OUT_CDATA), .PC_OUT_CADDR(PC_OUT_CADDR), .A_LD_CDATA(A_LD_CDATA),
    .A_OUT_CDATA(A_OUT_CDATA), .X_LD_CDATA(X_LD_CDATA), .X_OUT_CDATA(X_OUT_CDATA), .PZ_LD(PZ_LD),
    .ALUA_LD_CDATA(ALUA_LD_CDATA), .ALUB_LD_CDATA(ALUB_LD_CDATA), .ALUR_OUT_CDATA(ALUR_OUT_CDATA),
    .ALUOP_0(ALUOP_0), .ALUOP_1(ALUOP_1), .Z_SRC_CDATA(Z_SRC_CDATA), .CPU_ERR(CPU_ERR),
    .lt_CAR_gt(lt_CAR_gt), .lt_UPARAM_gt(lt_UPARAM_gt), .lt_CARNEXT_gt(lt_CARNEXT_gt),
    .lt_CARNEXTSRC_gt(lt_CARNEXTSRC_gt));
  Seven_Seg_Hex seven_seg_hex_33 (.d(MCBREAKPOINT[7:4]), .dp(1'b0));
  Seven_Seg_Hex seven_seg_hex_34 (.d(UCBREAKPOINT[7:4]), .dp(1'b0));
  Seven_Seg_Hex seven_seg_hex_35 (.d(MCBREAKPOINT[3:0]), .dp(1'b0));
  Seven_Seg_Hex seven_seg_hex_36 (.d(UCBREAKPOINT[3:0]), .dp(1'b0));
  PullDown #(.Bits(8)) pulldown_4 (.out(ALUR));
  // PC PC: pin names not known; wires that end beside it: PC_LD_CDATA, PC_INC, PC_REL_CDATA, ALUR, CLOCK, {FROMPC7, FROMPC6, FROMPC5, FROMPC4, FROMPC3, FROMPC2, FROMPC1, FROMPC0}
  _7432 Load_control__Or (
    .pin1(1'b0), .pin2(1'b0), .pin4(1'b0), .pin5(1'b0), .pin7(1'b0), .pin9(1'b0), .pin10(1'b0),
    .pin11(Load_control__Or_pin11), .pin12(MBR_LD_XDATA), .pin13(MBR_LD_CDATA), .pin14(1'b1));  // open: pin3, pin6, pin8
  _74244 Route_to_XDATA__Tristate (
    .pin1(Route_to_XDATA__Tristate_pin1), .pin2(FROMMBR0), .pin3(FROMXDATA7), .pin4(FROMMBR1),
    .pin5(FROMXDATA6), .pin6(FROMMBR2), .pin7(FROMXDATA5), .pin8(FROMMBR3), .pin9(FROMXDATA4), .pin10(1'b0),
    .pin11(FROMMBR4), .pin12(FROMXDATA3), .pin13(FROMMBR5), .pin14(FROMXDATA2), .pin15(FROMMBR6),
    .pin16(FROMXDATA1), .pin17(FROMMBR7), .pin18(FROMXDATA0), .pin19(Route_to_XDATA__Tristate_pin1),
    .pin20(1'b1));
  _74244 Connect_CDATA_to_CADDR__Tristate (
    .pin1(Connect_CDATA_to_CADDR__Tristate_pin1), .pin2(ALUR[0]), .pin3(CADDR[7]), .pin4(ALUR[1]),
    .pin5(CADDR[6]), .pin6(ALUR[2]), .pin7(CADDR[5]), .pin8(ALUR[3]), .pin9(CADDR[4]), .pin10(1'b0),
    .pin11(ALUR[4]), .pin12(CADDR[3]), .pin13(ALUR[5]), .pin14(CADDR[2]), .pin15(ALUR[6]), .pin16(CADDR[1]),
    .pin17(ALUR[7]), .pin18(CADDR[0]), .pin19(Connect_CDATA_to_CADDR__Tristate_pin1), .pin20(1'b1));
  _74157 Load_from_XDATA_CDATA_low__MUX (
    .pin1(MBR_LD_CDATA), .pin2(FROMXDATA0), .pin3(ALUR[0]), .pin4(FROMXCDATA0), .pin5(FROMXDATA1),
    .pin6(ALUR[1]), .pin7(FROMXCDATA1), .pin8(1'b0), .pin9(FROMXCDATA2), .pin10(ALUR[2]), .pin11(FROMXDATA2),
    .pin12(FROMXCDATA3), .pin13(ALUR[3]), .pin14(FROMXDATA3), .pin15(1'b0), .pin16(1'b1));
  _74244 Route_to_CADDR__Tristate (
    .pin1(Route_to_CADDR__Tristate_pin1), .pin2(FROMPC0), .pin3(CADDR[7]), .pin4(FROMPC1), .pin5(CADDR[6]),
    .pin6(FROMPC2), .pin7(CADDR[5]), .pin8(FROMPC3), .pin9(CADDR[4]), .pin10(1'b0), .pin11(FROMPC4),
    .pin12(CADDR[3]), .pin13(FROMPC5), .pin14(CADDR[2]), .pin15(FROMPC6), .pin16(CADDR[1]), .pin17(FROMPC7),
    .pin18(CADDR[0]), .pin19(Route_to_CADDR__Tristate_pin1), .pin20(1'b1));
  _7404 Not (
    .pin1(CDATA_TO_CADDR), .pin2(Connect_CDATA_to_CADDR__Tristate_pin1), .pin3(1'b0), .pin5(1'b0),
    .pin7(1'b0), .pin9(1'b0), .pin11(1'b0), .pin12(Not_pin12), .pin13(CDATA_LD_0), .pin14(1'b1));  // open: pin4, pin6, pin8, pin10
  _7404 Not_2 (
    .pin1(MBR_OUT_XDATA), .pin2(Route_to_XDATA__Tristate_pin1), .pin3(Load_control__Or_pin11),
    .pin4(Not_2_pin4), .pin5(1'b0), .pin7(1'b0), .pin9(1'b0), .pin11(1'b0), .pin12(Not_2_pin12),
    .pin13(MBR_OUT_CDATA), .pin14(1'b1));  // open: pin6, pin8, pin10
  _7404 Not_3 (
    .pin1(PC_OUT_CADDR), .pin2(Route_to_CADDR__Tristate_pin1), .pin3(1'b0), .pin5(1'b0), .pin7(1'b0),
    .pin9(1'b0), .pin11(1'b0), .pin12(Not_3_pin12), .pin13(PC_OUT_CDATA), .pin14(1'b1));  // open: pin4, pin6, pin8, pin10
  _74377 _74377_1 (
    .pin1(Not_2_pin4), .pin2(FROMMBR0), .pin3(FROMXCDATA0), .pin4(FROMXCDATA1), .pin5(FROMMBR1),
    .pin6(FROMMBR2), .pin7(FROMXCDATA2), .pin8(FROMXCDATA3), .pin9(FROMMBR3), .pin10(1'b0), .pin11(CLOCK),
    .pin12(FROMMBR4), .pin13(FROMXCDATA4), .pin14(FROMXCDATA5), .pin15(FROMMBR5), .pin16(FROMMBR6),
    .pin17(FROMXCDATA6), .pin18(FROMXCDATA7), .pin19(FROMMBR7), .pin20(1'b1));
  _74244 Pull_CDATA_to_Zero (
    .pin1(Not_pin12), .pin2(1'b0), .pin3(ALUR[7]), .pin4(1'b0), .pin5(ALUR[6]), .pin6(1'b0), .pin7(ALUR[5]),
    .pin8(1'b0), .pin9(ALUR[4]), .pin10(1'b0), .pin11(1'b0), .pin12(ALUR[3]), .pin13(1'b0), .pin14(ALUR[2]),
    .pin15(1'b0), .pin16(ALUR[1]), .pin17(1'b0), .pin18(ALUR[0]), .pin19(Not_pin12), .pin20(1'b1));
  _74157 Load_from_XDATA_CDATA_high__MUX (
    .pin1(MBR_LD_CDATA), .pin2(FROMXDATA4), .pin3(ALUR[4]), .pin4(FROMXCDATA4), .pin5(FROMXDATA5),
    .pin6(ALUR[5]), .pin7(FROMXCDATA5), .pin8(1'b0), .pin9(FROMXCDATA6), .pin10(ALUR[6]), .pin11(FROMXDATA6),
    .pin12(FROMXCDATA7), .pin13(ALUR[7]), .pin14(FROMXDATA7), .pin15(1'b0), .pin16(1'b1));
  _74244 Route_to_CDATA__Tristate (
    .pin1(Not_2_pin12), .pin2(FROMMBR0), .pin3(ALUR[7]), .pin4(FROMMBR1), .pin5(ALUR[6]), .pin6(FROMMBR2),
    .pin7(ALUR[5]), .pin8(FROMMBR3), .pin9(ALUR[4]), .pin10(1'b0), .pin11(FROMMBR4), .pin12(ALUR[3]),
    .pin13(FROMMBR5), .pin14(ALUR[2]), .pin15(FROMMBR6), .pin16(ALUR[1]), .pin17(FROMMBR7), .pin18(ALUR[0]),
    .pin19(Not_2_pin12), .pin20(1'b1));
  _74244 Route_to_CDATA__Tristate_2 (
    .pin1(Not_3_pin12), .pin2(FROMPC0), .pin3(ALUR[7]), .pin4(FROMPC1), .pin5(ALUR[6]), .pin6(FROMPC2),
    .pin7(ALUR[5]), .pin8(FROMPC3), .pin9(ALUR[4]), .pin10(1'b0), .pin11(FROMPC4), .pin12(ALUR[3]),
    .pin13(FROMPC5), .pin14(ALUR[2]), .pin15(FROMPC6), .pin16(ALUR[1]), .pin17(FROMPC7), .pin18(ALUR[0]),
    .pin19(Not_3_pin12), .pin20(1'b1));

  // Other names for the same wires on the sheet: XDATA_CDATA[7:0] = {FROMXCDATA7, FROMXCDATA6, FROMXCDATA5, FROMXCDATA4, FROMXCDATA3, FROMXCDATA2, FROMXCDATA1, FROMXCDATA0};
  //   MBR[7:0] = {FROMMBR7, FROMMBR6, FROMMBR5, FROMMBR4, FROMMBR3, FROMMBR2, FROMMBR1, FROMMBR0};
  //   PC[7:0] = {FROMPC7, FROMPC6, FROMPC5, FROMPC4, FROMPC3, FROMPC2, FROMPC1, FROMPC0}; TOCADDR0 = CADDR[0];
  //   TOCADDR1 = CADDR[1]; TOCADDR2 = CADDR[2]; TOCADDR3 = CADDR[3]; TOCADDR4 = CADDR[4]; TOCADDR5 = CADDR[5];
  //   TOCADDR6 = CADDR[6]; TOCADDR7 = CADDR[7]; CDATA[7:0] = ALUR; FROMCDATA0 = ALUR[0]; TOCDATA0 = ALUR[0];
  //   FROMCDATA1 = ALUR[1]; TOCDATA1 = ALUR[1]; FROMCDATA2 = ALUR[2]; TOCDATA2 = ALUR[2]; FROMCDATA3 = ALUR[3];
  //   TOCDATA3 = ALUR[3]; FROMCDATA4 = ALUR[4]; TOCDATA4 = ALUR[4]; FROMCDATA5 = ALUR[5]; TOCDATA5 = ALUR[5];
  //   FROMCDATA6 = ALUR[6]; TOCDATA6 = ALUR[6]; FROMCDATA7 = ALUR[7]; TOCDATA7 = ALUR[7]; TOXDATA0 = FROMXDATA0;
  //   XDATA[7:0] = {FROMXDATA7, FROMXDATA6, FROMXDATA5, FROMXDATA4, FROMXDATA3, FROMXDATA2, FROMXDATA1, FROMXDATA0};
  //   TOXDATA1 = FROMXDATA1; TOXDATA2 = FROMXDATA2; TOXDATA3 = FROMXDATA3; TOXDATA4 = FROMXDATA4;
  //   TOXDATA5 = FROMXDATA5; TOXDATA6 = FROMXDATA6; TOXDATA7 = FROMXDATA7; XADDR[7:0] = MAR

  // Notes on the sheet:
  //   MCBREAKPOINT: default 16
  //   UCBREAKPOINT: default 18
  //   FAST: Hz: 500
  //   SLOW: Hz: 50
  //   Clock
  //   Breakpoints
  //   Error Conditions
  //   CPU
  //   MAR
  //   A
  //   MBR
  //   X
  //   PC
  //   IR
  //   P
  //   Z
  //   XADDR Bus
  //   CADDR Bus
  //   Bank Selection
  //   Instruction Decoder
  //   (p1) MODEADDR
  //   ALU
  //   ALUA
  //   ALUB
  //   ALUOUT
  //   I think there is an error in the RAM write select.
  //   If the clock is still high after a cycle and mem/ld/xdata goes high
  //   And CS is high then the data will latch!
  //   Is the solution to actually have clock directly
  //   attached to WE (latch on rising edge only)
  //   Then have CS be CS1 AND (MEM/LD/XDATA or MEM/OUT/XDATA)
  //   (p2) OPCODEADDR
  //   ROM/RAM Banks
  //   OP
  //   Control Unit
  //   CAR
  //   contents of ROM (hex, n*v repeats v):
  //   a9,42,16379*0,2
  //   XDATA Bus
  //   CARNEXT
  //   UPARAM
  //   I/O
  //   CARNEXTSRC
  //   POST1
  //   POST0
  //   ALU operation
  //   0 0 ADD
  //   0 1 SUB
  //   1 0 INC
  //   1 1 DEC
  //   General Purpose Registers
  //   HALTED
  //   ERROR
  //   BREAKPOINT
  //   MC Breakpoint
  //   UC Breakpoint
  //   CDATA Bus
  //   Progam Counter
  //   Bus Control
  //   NOTES
  //   This routing is only used for stack operations 
  //   and so can be dropped for now
  //   Used for initialisation/reset
endmodule
