// Digital circuit Io-no-addr-decoder.dig as structural Verilog
module Io_no_addr_decoder (
  input  [7:0] ADDR,
  input  [7:0] IN,
  input  WR,
  input  CLK
);

  wire and_1_out, comparator_1_eq;

  Comparator #(.Bits(8)) comparator_1 (.a(ADDR), .b(8'hfe), .eq(comparator_1_eq));  // open: gt, lt
  and and_1 (and_1_out, comparator_1_eq, WR);
  Terminal terminal_1 (.D(IN), .C(CLK), .en(and_1_out));

  // Other names for the same wires on the sheet: Clck1 = CLK

  // Notes on the sheet:
  //   ADDR
  //   0xF2 Write to terminal
  //   Terminal
endmodule
